# Fritzing sketch air-quality (saved by Fritzing 1.0.2b)
breadboards: 2

parts:
  Mod1 = Amica NodeMCU DEVKIT 1.0
  Part1 = OLED Monochrome 128x64 0.96 inch [part_number=326]
  DHT1 = DHT22 Humidity and Temperature Sensor
  DS1 = DS18B20 1-Wire Temperature Sensor [part_number=DS18B20]
  DS2 = DS18B20 1-Wire Temperature Sensor [part_number=DS18B20]
  DS3 = DS18B20 1-Wire Temperature Sensor [part_number=DS18B20]
  DS4 = DS18B20 1-Wire Temperature Sensor [part_number=DS18B20]
  DS5 = DS18B20 1-Wire Temperature Sensor [part_number=DS18B20]
  DS6 = DS18B20 1-Wire Temperature Sensor [part_number=DS18B20]
  DS7 = DS18B20 1-Wire Temperature Sensor [part_number=DS18B20]
  DS8 = DS18B20 1-Wire Temperature Sensor [part_number=DS18B20]
  Part3 = Barometric Pressure Sensor - BMP180 Breakout (GY-68)
  Part4 = MQ-9 breakout
  R1 = Resistor [tolerance=±5% power=0.25W resistance=4.7k package=THT]

nets:
  VDD: Mod1.pin1, Mod1.pin_10, Mod1.pin_26, Part1.VIN, DHT1.VDD, DS1.VDD, DS2.VDD, DS3.VDD, DS4.VDD, DS5.VDD, DS6.VDD, DS7.VDD, DS8.VDD, Part3.VCC, Part4.VCC
  GND: Mod1.pin2, Mod1.pin_9, Mod1.pin_25, Mod1.pin_29, Part1.GND, DHT1.GND, DS1.GND, DS2.GND, DS3.GND, DS4.GND, DS5.GND, DS6.GND, DS7.GND, DS8.GND, Part3.GND, Part4.GND, R1.Pin_1
  N1: Mod1.pin7, DHT1.DATA
  N2: Mod1.pin_11, DS1.DQ, DS2.DQ, DS3.DQ, DS4.DQ, DS5.DQ, DS6.DQ, DS7.DQ, DS8.DQ, R1.Pin_0
  N3: Mod1.pin_13, Part1.MOSI_SDA, Part3.SDA
  N4: Mod1.pin_14, Part1.SCLK_SCK, Part3.SCL
  N5: Mod1.pin_15, Part4.DO
  N6: Mod1.pin_16, Part4.AO

custom parts:
  OLED Monochrome 128x64 0.96 inch: These displays are small, only about 1" diameter, but very readable due to the high contrast of an OLED display. This display is made of 128x64 individual white OLED pixels, each one is turned on or off by the controller chip. Because the display makes its own light, no backlight is required. This reduces the power required to run the OLED and is why the display has such high contrast; we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
  MQ-9 breakout: SKU: 101284
